# Fritzing sketch pcb (saved by Fritzing 0.9.3b)
circuit board: 4.6cm x 4.3cm
breadboards: 1

parts:
  R1 = Resistor [tolerance=±5% resistance=470 package=THT]
  R2 = Resistor [tolerance=±5% resistance=220 package=THT]
  J1 = female pin header, 8 pins [form="♀ (female)" part_number=D5-D12]
  J2 = female pin header, 7 pins [form="♀ (female)" part_number=GND-A4]
  J3 = female pin header, 4 pins [form="♀ (female)" part_number=DISPLAY]
  J4 = female pin header, 4 pins [form="♀ (female)" part_number=RTC]
  PUSH = female pin header, 3 pins [form="♀ (female)"]
  LED = female pin header, 2 pins [form="♀ (female)"]
  GND = female pin header, 2 pins [form="♀ (female)"]
  GND_2 = female pin header, 3 pins [form="♀ (female)"]

nets:
  N1: R1.Pin_0, J1.pin8
  N2: R1.Pin_1, LED.pin2
  N3: R2.Pin_0, J1.pin7
  N4: R2.Pin_1, LED.pin1
  N5: J1.pin1, J3.pin1
  N6: J1.pin2, J3.pin2
  N7: J1.pin3, PUSH.pin1
  N8: J1.pin4, PUSH.pin2
  N9: J1.pin5, PUSH.pin3
  N10: J2.pin1, J4.pin2
  N11: J2.pin2, J4.pin1
  N12: J2.pin5, J3.pin3, J4.pin3
  N13: J2.pin7, J3.pin4, J4.pin4, GND.pin1, GND.pin2, GND_2.pin1, GND_2.pin2, GND_2.pin3

notes:
  PLUS
  MINUS
  MODE
  CLK
  DIO
  VCC
  GND
  SCL
  SDA
  RED
  BLUE
  Maxalarm Clock
  v1.0
  Arduino Nano
  D12
