# Fritzing sketch schematic (saved by Fritzing 0.9.3b)
breadboards: 1

parts:
  Part3 = Real Time Clock Module - DS1307 RTC Breakout Board
  S2 = Pushbutton [package="[SMD]"]
  LED1 = LED - 3mm [color="Red (633nm)" package="3 mm [THT]"]
  LED2 = LED - 3mm [color="Blue (430nm)" package="3 mm [THT]"]
  U2 = 74HC595 [package="DIP16 [THT]"]
  S3 = Pushbutton [package="[SMD]"]
  R2 = Resistor [tolerance=±5% resistance=1k package=THT]
  R3 = Resistor [tolerance=±5% resistance=1k package=THT]
  R4 = Resistor [tolerance=±5% resistance=1k package=THT]
  R5 = Resistor [tolerance=±5% resistance=1k package=THT]
  R6 = Resistor [tolerance=±5% resistance=1k package=THT]
  R7 = Resistor [tolerance=±5% resistance=1k package=THT]
  R8 = Resistor [tolerance=±5% resistance=1k package=THT]
  Part4 = Arduino Nano (Rev3.0) (ICSP)
  U1 = 7-SEGMENT-4DIGIT-YOUNGSUN [package=7-segment-4digit-youngsun]
  S1 = Pushbutton [package="[THT]"]
  R1 = Resistor [tolerance=±5% resistance=1k package=THT]

nets:
  5V: Part3.5V, U2.VCC, Part4.5V
  GND: Part3.GND, S2.Pin_3, S2.Pin_4, LED1.cathode, LED2.cathode, U2.GND, U2.OE, S3.Pin_3, S3.Pin_4, Part4.GND, S1.Pin_3, S1.Pin_4
  N1: Part3.SCL, Part4.A5
  N2: Part3.SDA, Part4.A4
  N3: S2.Pin_1, S2.Pin_2, Part4.D11/MOSI
  N4: LED1.anode, Part4.A2
  N5: LED2.anode, Part4.A3
  N6: U2.Q1, R6.Pin_1
  N7: U2.Q2, R8.Pin_1
  N8: U2.Q3, R5.Pin_1
  N9: U2.Q4, R3.Pin_1
  N10: U2.Q5, R4.Pin_1
  N11: U2.Q6, R2.Pin_1
  N12: U2.Q7, R1.Pin_1
  N13: U2.SH_CP, Part4.D8
  N14: U2.ST_CP, Part4.D6
  N15: U2.DS, Part4.D7
  N16: U2.Q0, R7.Pin_1
  N17: S3.Pin_1, S3.Pin_2, Part4.D9
  N18: R2.Pin_0, U1.G
  N19: R3.Pin_0, U1.E
  N20: R4.Pin_0, U1.F
  N21: R5.Pin_0, U1.D
  N22: R6.Pin_0, U1.B
  N23: R7.Pin_0, U1.A
  N24: R8.Pin_0, U1.C
  N25: Part4.D2, U1.DIG1
  N26: Part4.D3, U1.DIG2
  N27: Part4.D4, U1.DIG3
  N28: Part4.D5, U1.DIG4
  N29: Part4.D10, S1.Pin_1, S1.Pin_2
  N30: U1.DP, R1.Pin_0
