# Fritzing sketch soldered-prototype (saved by Fritzing 0.9.3b)
perfboards: 1

parts:
  Blue_LED_connector = Screw terminal - 2 pins [package=THT]
  Red_LED_connector = Screw terminal - 2 pins [package=THT]
  R1 = Resistor [tolerance=±5% resistance=220 package=THT]
  R2 = Resistor [tolerance=±5% resistance=44 package=THT]
  MODE_SW1 = Pushbutton [package="[THT]"]
  MODE_SW2 = Pushbutton [package="[THT]"]
  MODE_SW3 = Pushbutton [package="[THT]"]
  Part1 = Arduino Nano (Rev3.0)

nets:
  N1: Blue_LED_connector.pin1, R2.Pin_0
  N2: Blue_LED_connector.pin2, Red_LED_connector.pin2, MODE_SW1.Pin_3, MODE_SW1.Pin_4, MODE_SW2.Pin_3, MODE_SW2.Pin_4, MODE_SW3.Pin_3, MODE_SW3.Pin_4, Part1.GND
  N3: Red_LED_connector.pin1, R1.Pin_0
  N4: MODE_SW1.Pin_1, MODE_SW1.Pin_2, Part1.D8
  N5: MODE_SW2.Pin_1, MODE_SW2.Pin_2, Part1.D9
  N6: MODE_SW3.Pin_1, MODE_SW3.Pin_2, Part1.D10

notes:
  Pin socket to RTC
  Pin socket to display
